# Fritzing sketch Schematics (saved by Fritzing 0.9.4)

parts:
  WeMos_D1_Mini1 = WeMos D1 Mini
  Squix1 = OLED 0.91" 128x32 I2C SSD1306 (GND/VCC)
  Relay_5V1 = Keyes Relay [package=THT]
  Part1 = RF-MODULE 315/433 [package=rf-link_rx]
  PIR1 = PIR sensor
  C1_470mF = Electrolytic Capacitor [capacitance=47µF voltage=16V package="100 mil [THT, electrolytic]"]
  R1 = Photocell (LDR) [package=THT]
  C3_104 = Ceramic Capacitor [capacitance=0.1mF package="100 mil [THT, multilayer]"]  # not connected
  C4_104 = Ceramic Capacitor [capacitance=0.1mF package="100 mil [THT, multilayer]"]
  C2_470mF = Electrolytic Capacitor [capacitance=47µF voltage=16V package="0405 [SMD, electrolytic]"]  # not connected
  R2 = Resistor [tolerance=±5% resistance=220 package=THT]
  Thermistor = Temperature Sensor (Thermistor) [thermistor_type=NTC package=THT]
  Ther = V18ZA2P [package=v18za2p]  # not connected
  F1 = FUSE [package=fuse_5mm]
  HLK-PM1 = HLK-PM01
  LED1 = LEDs [package=led10mm]

nets:
  N1: WeMos_D1_Mini1.5V, HLK-PM1.+Vo
  N2: WeMos_D1_Mini1.A0, R1.pin_0, R2.Pin_0
  N3: WeMos_D1_Mini1.D0, PIR1.SIG, C4_104.1
  N4: WeMos_D1_Mini1.D1, Squix1.SCL
  N5: WeMos_D1_Mini1.D2, Squix1.SCA
  N6: WeMos_D1_Mini1.D6, Part1.Data
  N7: WeMos_D1_Mini1.D7, Relay_5V1.ground
  N8: WeMos_D1_Mini1.G, HLK-PM1.-Vo
  N9: Relay_5V1.power, C1_470mF.-
  N10: Relay_5V1.NO, F1.2
  N11: Thermistor.pin_0, LED1.A
  N12: Thermistor.pin_1, F1.1
  N13: HLK-PM1.AC#0, LED1.C

custom parts:
  OLED 0.91" 128x32 I2C SSD1306 (GND/VCC): OLED 0.91" 128x32 I2C SSD1306 Pinout: GND/VCC/SCL/SDA
  Keyes Relay: The Keyes 5V relay module is suitable for SCM development, home appliance control. It uses a 5V~12V TIL control signal which can control DC / AC signal.
  RF-MODULE 315/433: RF Link receivers- WRL-8947, 8948, 8949, 8950
  LEDs: LEDs Standard schematic elements and footprints for 5mm, 3mm, 1206, and 0603 sized LEDs. 5mm - Spark Fun Electronics SKU : COM-00529 (and others)
